// Logisim project LeMinhChi_6551071011_C6.circ as structural Verilog: 1 circuit, main circuit main
module main (
  input  Reset,
  input  Enable,
  output Q3,
  output Q2,
  output Q1,
  output Q0
);

  wire clock_1_out, j_k_ff_1_qn;

  Clock clock_1 (.out(clock_1_out));
  J_K_Flip_Flop #(.trigger("falling")) j_k_ff_1 (
    .J(Enable), .Q(Q3), .Qn(j_k_ff_1_qn));  // open: clk, K, preset, en, reset
  J_K_Flip_Flop #(.trigger("falling")) j_k_ff_2 (.J(Enable), .K(Reset), .Q(Q2));  // open: clk, Qn, preset, en, reset
  J_K_Flip_Flop #(.trigger("falling")) j_k_ff_3 (.J(Enable), .Q(Q1));  // open: clk, K, Qn, preset, en, reset
  J_K_Flip_Flop #(.trigger("falling")) j_k_ff_4 (
    .J(Enable), .clk(clock_1_out), .Q(Q0));  // open: K, Qn, preset, en, reset
endmodule
